// Logisim project g1.circ as structural Verilog: 9 circuits, main circuit main
module main (
  output Instruccion_R,
  output addi,
  output jump,
  output load,
  output store,
  output beq,
  output [4:0] rd,
  output [4:0] shampt,
  output [25:0] jump_2,
  output [15:0] offset
);

  wire alusrc, Branch, button_1_out, Clock, MemtoReg, not_1_out, Regdst, RegW, Reset, salida, UC_menread,
       UC_menwrite, Zero;
  wire [1:0] UC_aluop;
  wire [3:0] ALUcontrol_out_3, or_2_out;
  wire [4:0] Decodificador_rs, Decodificador_rt, multiplexer_2_out;
  wire [5:0] Decodificador_funct, Decodificador_op;
  wire [23:0] bit_extender_2_out, pc_1_pc;
  wire [31:0] ALU_out_4, bit_extender_1_out, multiplexer_1_out, multiplexer_3_out, ram_1_data, ram_2_data,
       Registros_r_rs, Registros_r_rt;

  // Probe on pc_1_pc
  PC pc_1 (
    .DirJump(jump_2), .Clk(Clock), .Reset(Reset), .Offset(offset), .Jump(jump), .Branch(Branch), .Zero(Zero),
    .Pc(pc_1_pc));
  Adder #(.width(32)) adder_1 ();  // open: a, b, out, cin, cout
  RAM #(.addrWidth(24), .dataWidth(32)) ram_1 (
    .addr(pc_1_pc), .data(ram_1_data), .sel(1'b1), .clk(Clock), .clr(button_1_out));  // open: ld
  Button button_1 (.out(button_1_out));
  Clock clock_1 (.out(Clock));
  Button button_2 (.out(Reset));
  Dedodificador Decodificador (
    .Entrada_Instruccion(ram_1_data), .op(Decodificador_op), .rs(Decodificador_rs), .rt(Decodificador_rt),
    .rd(rd), .shampt(shampt), .funct(Decodificador_funct), .Jump(jump_2), .Immediate_offset(offset));
  memoria Registros (
    .CLOCK(Clock), .R_rs(Registros_r_rs), .rs(Decodificador_rs), .R_rt(Registros_r_rt),
    .rt(Decodificador_rt), .cod(multiplexer_2_out), .dato(multiplexer_3_out), .Regwrite(RegW), .Reset(Reset));
  // Probe on Decodificador_rs
  assign bit_extender_1_out = {{16{1'b0}}, offset};  // Bit_Extender bit_extender_1
  datapath datapath_1 (
    .in_1(Decodificador_op), .Instruction_type_R(Instruccion_R), .Addi(addi), .JUMP(jump), .LOAD_HW(load),
    .STORE(store), .BEQ(beq));
  // Probe on UC_aluop
  Multiplexer #(.width(32)) multiplexer_1 (
    .in0(Registros_r_rt), .in1(bit_extender_1_out), .out(multiplexer_1_out), .sel(alusrc));  // open: en
  UnidadControl UC (
    .ADDI(addi), .OP(Decodificador_op), .RegDst(Regdst), .AluSrc(alusrc), .MentoReg(MemtoReg),
    .RegWrite(RegW), .MenRead(UC_menread), .MenWrite(UC_menwrite), .Branch(Branch), .ALUOp(UC_aluop));  // open: TipoR
  Multiplexer #(.width(5)) multiplexer_2 (
    .in0(Decodificador_rt), .in1(rd), .out(multiplexer_2_out), .sel(Regdst));  // open: en
  // Probe on multiplexer_2_out
  ALUcontrol ALUcontrol (.ALUOp(UC_aluop), .funct(Decodificador_funct), .out_3(ALUcontrol_out_3));
  // Probe on Decodificador_funct
  or or_1 (salida, addi, load, store);
  ALU ALU (.A(Registros_r_rs), .B(multiplexer_1_out), .AluControl(or_2_out), .out_4(ALU_out_4), .Zero(Zero));
  Bit_Extender #(.in_width(32), .out_width(24)) bit_extender_2 (.in(ALU_out_4), .out(bit_extender_2_out));
  assign or_2_out = ALUcontrol_out_3 | {4{Branch}} | {{2{ALUcontrol_out_3[3]}}, salida, ALUcontrol_out_3[3]};  // OR_Gate or_2, 4 bits wide
  not not_1 (not_1_out, Clock);
  RAM #(.addrWidth(24), .dataWidth(32), .bus("separate")) ram_2 (
    .addr(bit_extender_2_out), .din(Registros_r_rt), .data(ram_2_data), .str(UC_menwrite), .clk(not_1_out),
    .ld(UC_menread), .clr(Reset));  // open: sel
  Multiplexer #(.width(32)) multiplexer_3 (
    .in0(ALU_out_4), .in1(ram_2_data), .out(multiplexer_3_out), .sel(MemtoReg));  // open: en

  // Other names for the same wires on the sheet: DirJump[25:0] = jump_2
endmodule

module rama (
  input  [15:0] in_1
);

  wire and_1_out, branch, Zero;
  wire [23:0] adder_1_out, bit_extender_1_out, multiplexer_1_out, pc_1, subtractor_1_out;

  assign bit_extender_1_out = {{9{1'b0}}, in_1[14:0]};  // Bit_Extender bit_extender_1
  Adder #(.width(24)) adder_1 (.a(pc_1), .b(bit_extender_1_out), .out(adder_1_out));  // open: cin, cout
  Subtractor #(.width(24)) subtractor_1 (.a(pc_1), .b(bit_extender_1_out), .out(subtractor_1_out));  // open: bin, bout
  Multiplexer #(.width(24), .enable("false")) multiplexer_1 (
    .in0(adder_1_out), .in1(subtractor_1_out), .out(multiplexer_1_out), .sel(in_1[15]));
  Multiplexer #(.width(24), .enable("false")) multiplexer_2 (
    .in0(pc_1), .in1(multiplexer_1_out), .sel(and_1_out));  // open: out
  and and_1 (and_1_out, Zero, branch);

  // Other names for the same wires on the sheet: imm[15:0] = in_1

  // Notes on the sheet:
  //   Branch
endmodule

module PC (
  input  [25:0] DirJump,
  input  Clk,
  input  Reset,
  input  [15:0] Offset,
  input  Jump,
  input  Branch,
  input  Zero,
  output [23:0] Pc
);

  wire and_1_out;
  wire [23:0] adder_1_out, adder_2_out, bit_extender_1_out, multiplexer_1_out, multiplexer_2_out,
       multiplexer_3_out, subtractor_1_out;

  Register #(.width(24)) u_Pc (.D(multiplexer_3_out), .en(Clk), .Q(Pc), .clk(Clk), .clr(Reset));
  assign bit_extender_1_out = {{9{1'b0}}, Offset[14:0]};  // Bit_Extender bit_extender_1
  Adder #(.width(24)) adder_1 (.a(Pc), .b(24'h1), .out(adder_1_out));  // open: cin, cout
  Adder #(.width(24)) adder_2 (.a(adder_1_out), .b(bit_extender_1_out), .out(adder_2_out));  // open: cin, cout
  Subtractor #(.width(24)) subtractor_1 (
    .a(adder_1_out), .b(bit_extender_1_out), .out(subtractor_1_out));  // open: bin, bout
  Multiplexer #(.width(24), .enable("false")) multiplexer_1 (
    .in0(adder_2_out), .in1(subtractor_1_out), .out(multiplexer_1_out), .sel(Offset[15]));
  Multiplexer #(.width(24), .enable("false")) multiplexer_2 (
    .in0(adder_1_out), .in1(multiplexer_1_out), .out(multiplexer_2_out), .sel(and_1_out));
  and and_1 (and_1_out, Branch, Zero);
  Multiplexer #(.width(24), .enable("false")) multiplexer_3 (
    .in0(multiplexer_2_out), .in1(DirJump[23:0]), .out(multiplexer_3_out), .sel(Jump));
endmodule

module Dedodificador (
  input  [31:0] Entrada_Instruccion,
  output [5:0] op,
  output [4:0] rs,
  output [4:0] rt,
  output [4:0] rd,
  output [4:0] shampt,
  output [5:0] funct,
  output [25:0] Jump,
  output [15:0] Immediate_offset
);


  assign funct = Entrada_Instruccion[5:0];
  assign Immediate_offset = Entrada_Instruccion[15:0];
  assign Jump = Entrada_Instruccion[25:0];
  assign op = Entrada_Instruccion[31:26];
  assign rd = Entrada_Instruccion[15:11];
  assign rs = Entrada_Instruccion[25:21];
  assign rt = Entrada_Instruccion[20:16];
  assign shampt = Entrada_Instruccion[10:6];

  // Notes on the sheet:
  //   Instruccion tipo R
endmodule

module datapath (
  input  [5:0] in_1,
  output Instruction_type_R,
  output Addi,
  output JUMP,
  output LOAD_HW,
  output STORE,
  output BEQ
);

  Comparator #(.width(6)) comparator_1 (.a(in_1), .b({6{1'b0}}), .eq(Instruction_type_R));  // open: gt, lt
  Comparator #(.width(6)) comparator_2 (.a(in_1), .b(6'b001000), .eq(Addi));  // open: gt, lt
  Comparator #(.width(6)) comparator_3 (.a(in_1), .b(6'b000010), .eq(JUMP));  // open: gt, lt
  Comparator #(.width(6)) comparator_4 (.a(in_1), .b(6'b100011), .eq(LOAD_HW));  // open: gt, lt
  Comparator #(.width(6)) comparator_5 (.a(in_1), .b(6'b101011), .eq(STORE));  // open: gt, lt
  Comparator #(.width(6)) comparator_6 (.a(in_1), .b(6'b000100), .eq(BEQ));  // open: gt, lt
endmodule

module memoria (
  input  CLOCK,
  input  [4:0] rs,
  input  [4:0] rt,
  input  Reset,
  input  [4:0] cod,
  input  [31:0] dato,
  input  Regwrite,
  output [31:0] R_rs,
  output [31:0] R_rt
);

  wire _0A, _0B, _0C, _0D, _1A, _1B, _1C, _1D, _2A, _2B, _2C, _2D, _3A, _3B, _3C, _3D, _4A, _4B, _4C, _4D,
       _5A, _5B, _5C, _5D, _6A, _6B, _6C, _6D, _7A, _7B, _7C, _7D, and_1_out;
  wire [31:0] _0, _1, _2, _3, _4, _5, _6, _7, _8, _9, _10, _11, _12, _13, _14, _15, _16, _17, _18, _19, _20,
       _21, _22, _23, _24, _25, _26, _27, _28, _29, _30, _31;

  Multiplexer #(.select(5), .width(32)) multiplexer_1 (
    .in0(_0), .in1(_1), .in2(_2), .in3(_3), .in4(_4), .in5(_5), .in6(_6), .in7(_7), .in8(_8), .in9(_9),
    .in10(_10), .in11(_11), .in12(_12), .in13(_13), .in14(_14), .in15(_15), .in16(_16), .in17(_17),
    .in18(_18), .in19(_19), .in20(_20), .in21(_21), .in22(_22), .in23(_23), .in24(_24), .in25(_25),
    .in26(_26), .in27(_27), .in28(_28), .in29(_29), .in30(_30), .in31(_31), .out(R_rs), .sel(rs));  // open: en
  Multiplexer #(.select(5), .width(32)) multiplexer_2 (
    .in0(_0), .in1(_1), .in2(_2), .in3(_3), .in4(_4), .in5(_5), .in6(_6), .in7(_7), .in8(_8), .in9(_9),
    .in10(_10), .in11(_11), .in12(_12), .in13(_13), .in14(_14), .in15(_15), .in16(_16), .in17(_17),
    .in18(_18), .in19(_19), .in20(_20), .in21(_21), .in22(_22), .in23(_23), .in24(_24), .in25(_25),
    .in26(_26), .in27(_27), .in28(_28), .in29(_29), .in30(_30), .in31(_31), .out(R_rt), .sel(rt));  // open: en
  and and_1 (and_1_out, 1'b1, Regwrite);
  Demultiplexer #(.select(5)) demultiplexer_1 (
    .out0(_0A), .out1(_1A), .out2(_2A), .out3(_3A), .out4(_4A), .out5(_5A), .out6(_6A), .out7(_7A),
    .out8(_0B), .out9(_1B), .out10(_2B), .out11(_3B), .out12(_4B), .out13(_5B), .out14(_6B), .out15(_7B),
    .out16(_0C), .out17(_1C), .out18(_2C), .out19(_3C), .out20(_4C), .out21(_5C), .out22(_6C), .out23(_7C),
    .out24(_0D), .out25(_1D), .out26(_2D), .out27(_3D), .out28(_4D), .out29(_5D), .out30(_6D), .out31(_7D),
    .in(and_1_out), .sel(cod));  // open: en
  Register #(.width(32)) u__0 (.D(dato), .en(_0A), .Q(_0), .clk(CLOCK), .clr(Reset));
  Register #(.width(32)) u__8 (.D(dato), .en(_0B), .Q(_8), .clk(CLOCK), .clr(Reset));
  Register #(.width(32)) u__16 (.D(dato), .en(_0C), .Q(_16), .clk(CLOCK), .clr(Reset));
  Register #(.width(32)) u__24 (.D(dato), .en(_0D), .Q(_24), .clk(CLOCK), .clr(Reset));
  Register #(.width(32)) u__1 (.D(dato), .en(_1A), .Q(_1), .clk(CLOCK), .clr(Reset));
  Register #(.width(32)) u__9 (.D(dato), .en(_1B), .Q(_9), .clk(CLOCK), .clr(Reset));
  Register #(.width(32)) u__17 (.D(dato), .en(_1C), .Q(_17), .clk(CLOCK), .clr(Reset));
  Register #(.width(32)) u__25 (.D(dato), .en(_1D), .Q(_25), .clk(CLOCK), .clr(Reset));
  Register #(.width(32)) u__2 (.D(dato), .en(_2A), .Q(_2), .clk(CLOCK), .clr(Reset));
  Register #(.width(32)) u__10 (.D(dato), .en(_2B), .Q(_10), .clk(CLOCK), .clr(Reset));
  Register #(.width(32)) u__18 (.D(dato), .en(_2C), .Q(_18), .clk(CLOCK), .clr(Reset));
  Register #(.width(32)) u__26 (.D(dato), .en(_2D), .Q(_26), .clk(CLOCK), .clr(Reset));
  Register #(.width(32)) u__3 (.D(dato), .en(_3A), .Q(_3), .clk(CLOCK), .clr(Reset));
  Register #(.width(32)) u__11 (.D(dato), .en(_3B), .Q(_11), .clk(CLOCK), .clr(Reset));
  Register #(.width(32)) u__19 (.D(dato), .en(_3C), .Q(_19), .clk(CLOCK), .clr(Reset));
  Register #(.width(32)) u__27 (.D(dato), .en(_3D), .Q(_27), .clk(CLOCK), .clr(Reset));
  Register #(.width(32)) u__4 (.D(dato), .en(_4A), .Q(_4), .clk(CLOCK), .clr(Reset));
  Register #(.width(32)) u__12 (.D(dato), .en(_4B), .Q(_12), .clk(CLOCK), .clr(Reset));
  Register #(.width(32)) u__20 (.D(dato), .en(_4C), .Q(_20), .clk(CLOCK), .clr(Reset));
  Register #(.width(32)) u__28 (.D(dato), .en(_4D), .Q(_28), .clk(CLOCK), .clr(Reset));
  Register #(.width(32)) u__5 (.D(dato), .en(_5A), .Q(_5), .clk(CLOCK), .clr(Reset));
  Register #(.width(32)) u__13 (.D(dato), .en(_5B), .Q(_13), .clk(CLOCK), .clr(Reset));
  Register #(.width(32)) u__21 (.D(dato), .en(_5C), .Q(_21), .clk(CLOCK), .clr(Reset));
  Register #(.width(32)) u__29 (.D(dato), .en(_5D), .Q(_29), .clk(CLOCK), .clr(Reset));
  Register #(.width(32)) u__6 (.D(dato), .en(_6A), .Q(_6), .clk(CLOCK), .clr(Reset));
  Register #(.width(32)) u__14 (.D(dato), .en(_6B), .Q(_14), .clk(CLOCK), .clr(Reset));
  Register #(.width(32)) u__22 (.D(dato), .en(_6C), .Q(_22), .clk(CLOCK), .clr(Reset));
  Register #(.width(32)) u__30 (.D(dato), .en(_6D), .Q(_30), .clk(CLOCK), .clr(Reset));
  Register #(.width(32)) u__7 (.D(dato), .en(_7A), .Q(_7), .clk(CLOCK), .clr(Reset));
  Register #(.width(32)) u__15 (.D(dato), .en(_7B), .Q(_15), .clk(CLOCK), .clr(Reset));
  Register #(.width(32)) u__23 (.D(dato), .en(_7C), .Q(_23), .clk(CLOCK), .clr(Reset));
  Register #(.width(32)) u__31 (.D(dato), .en(_7D), .Q(_31), .clk(CLOCK), .clr(Reset));
endmodule

module UnidadControl (
  input  ADDI,
  input  [5:0] OP,
  output RegDst,
  output AluSrc,
  output MentoReg,
  output RegWrite,
  output MenRead,
  output MenWrite,
  output Branch,
  output TipoR,
  output [1:0] ALUOp
);

  wire and_1_out, and_2_out, and_3_out, and_4_out, not_1_out, not_2_out, not_3_out, not_4_out, not_5_out,
       not_6_out, not_7_out, not_8_out, not_9_out, not_10_out, not_11_out, not_12_out, not_13_out,
       not_14_out, not_15_out, not_16_out, not_17_out, not_18_out, not_19_out, not_20_out, not_21_out,
       not_22_out, not_23_out, not_24_out, not_25_out, not_26_out, not_27_out;

  Comparator #(.width(6)) comparator_1 (.a(OP), .b({6{1'b0}}), .eq(TipoR));  // open: gt, lt
  not not_1 (not_1_out, OP[1]);
  not not_2 (not_2_out, OP[2]);
  not not_3 (not_3_out, OP[4]);
  not not_4 (not_4_out, OP[5]);
  not not_5 (not_5_out, OP[5]);
  not not_6 (not_6_out, OP[4]);
  not not_7 (not_7_out, OP[2]);
  not not_8 (not_8_out, OP[1]);
  not not_9 (not_9_out, OP[0]);
  not not_10 (not_10_out, OP[3]);
  not not_11 (not_11_out, OP[1]);
  not not_12 (not_12_out, ADDI);
  and and_1 (and_1_out, not_1_out, not_2_out, OP[3], not_3_out, not_4_out);
  and and_2 (and_2_out, not_5_out, not_6_out, not_7_out, not_8_out, not_9_out);
  not not_13 (not_13_out, OP[3]);
  and and_3 (and_3_out, not_13_out, not_14_out);
  not not_14 (not_14_out, OP[2]);
  and and_4 (and_4_out, not_10_out, OP[1]);
  and and_5 (RegDst, not_11_out, not_12_out);
  or or_1 (AluSrc, OP[1], and_1_out);
  or or_2 (RegWrite, and_2_out, and_3_out);
  not not_15 (not_15_out, ADDI);
  and and_6 (MenWrite, OP[3], not_16_out);
  not not_16 (not_16_out, ADDI);
  not not_17 (not_17_out, OP[5]);
  not not_18 (not_18_out, OP[4]);
  not not_19 (not_19_out, OP[3]);
  not not_20 (not_20_out, OP[2]);
  not not_21 (not_21_out, OP[1]);
  not not_22 (not_22_out, OP[0]);
  not not_23 (not_23_out, OP[5]);
  not not_24 (not_24_out, OP[4]);
  not not_25 (not_25_out, OP[3]);
  not not_26 (not_26_out, OP[1]);
  not not_27 (not_27_out, OP[0]);
  and and_7 (MenRead, and_4_out, not_15_out);
  and and_8 (ALUOp[1], not_17_out, not_18_out, not_19_out, not_20_out, not_21_out, not_22_out);
  and and_9 (ALUOp[0], not_23_out, not_24_out, not_25_out, OP[2], not_26_out, not_27_out);

  assign Branch = OP[2];
  assign MentoReg = OP[1];
endmodule

module ALU (
  input  [31:0] A,
  input  [31:0] B,
  input  [3:0] AluControl,
  output [31:0] out_4,
  output Zero
);

  wire comparator_1_eq, comparator_2_eq, comparator_3_eq, comparator_4_eq;
  wire [2:0] priority_encoder_1_out;
  wire [31:0] add, \and , \or , Sub;

  Comparator #(.width(4)) comparator_1 (.a(AluControl), .b(4'b0010), .eq(comparator_1_eq));  // open: gt, lt
  Comparator #(.width(4)) comparator_2 (.a(AluControl), .b(4'b0110), .eq(comparator_2_eq));  // open: gt, lt
  Comparator #(.width(4)) comparator_3 (.a(AluControl), .b(4'b0000), .eq(comparator_3_eq));  // open: gt, lt
  Comparator #(.width(4)) comparator_4 (.a(AluControl), .b(4'b0001), .eq(comparator_4_eq));  // open: gt, lt
  Adder #(.width(32)) adder_1 (.a(A), .b(B), .out(add));  // open: cin, cout
  Subtractor #(.width(32)) subtractor_1 (.a(A), .b(B), .out(Sub));  // open: bin, bout
  Comparator #(.width(32)) comparator_5 (.a(A), .b(B), .eq(Zero));  // open: gt, lt
  Priority_Encoder priority_encoder_1 (
    .in0(comparator_1_eq), .in1(comparator_2_eq), .in2(comparator_3_eq), .in3(comparator_4_eq),
    .out(priority_encoder_1_out));  // open: in4, in5, in6, in7, en_in, gs, en_out
  assign \and  = A & B;  // AND_Gate and_1, 32 bits wide
  assign \or  = A | B;  // OR_Gate or_1, 32 bits wide
  Multiplexer #(.select(3), .width(32), .enable("false")) multiplexer_1 (
    .in0(add), .in1(Sub), .in2(\and ), .in3(\or ), .out(out_4), .sel(priority_encoder_1_out));  // open: in4, in5, in6, in7

  // Notes on the sheet:
  //   Add
  //   0010
  //   Substract
  //   0110
  //   and
  //   0000
  //   or
  //   0001
endmodule

module ALUcontrol (
  input  [1:0] ALUOp,
  input  [5:0] funct,
  output [3:0] out_3
);

  wire and_1_out, and_2_out, and_3_out, and_4_out, and_5_out, and_6_out, not_1_out, not_2_out, not_3_out,
       not_4_out, not_5_out, not_6_out, not_7_out, not_8_out;

  not not_1 (not_1_out, ALUOp[1]);
  not not_2 (not_2_out, funct[2]);
  not not_3 (not_3_out, ALUOp[1]);
  not not_4 (not_4_out, funct[2]);
  not not_5 (not_5_out, funct[3]);
  not not_6 (not_6_out, funct[1]);
  not not_7 (not_7_out, funct[2]);
  not not_8 (not_8_out, funct[0]);
  and and_1 (and_1_out, not_1_out, ALUOp[0]);
  and and_2 (and_2_out, ALUOp[1], not_2_out, funct[0]);
  and and_3 (and_3_out, ALUOp[1], funct[1]);
  and and_4 (and_4_out, ALUOp[1], funct[3]);
  or or_1 (out_3[1], not_3_out, not_4_out, funct[1], funct[3]);
  and and_5 (and_5_out, ALUOp[1], not_5_out, funct[2], not_6_out, funct[0]);
  and and_6 (and_6_out, ALUOp[1], funct[3], not_7_out, funct[1], not_8_out);
  or or_2 (out_3[2], and_1_out, and_2_out, and_3_out, and_4_out);
  or or_3 (out_3[0], and_5_out, and_6_out);

  assign out_3[3] = 1'b0;
endmodule
